# Fritzing sketch Arduino_Board-Sketch (saved by Fritzing 0.9.6b)
breadboards: 1

parts:
  Mod2 = KY-018 Photoresistor Module [package="Breakout board"]
  RTC2 = DS3231 AT24C32 Real Time Clock
  Part4 = Arduino Uno (Rev3)
  Part5 = DHT22 module
  TD-er2 = MH-Z19 CO2 sensor [part_number=MH-Z19]
  Capacitive_Soil_Moisture_Sensor2 = DFRobot Capacitive Soil Moisture Sensor V1.0 [part_number=SEN0193]

nets:
  VCC: Mod2.Vin, RTC2.VCC, Part4.3V3, Part5.VCC, Capacitive_Soil_Moisture_Sensor2.VCC
  GND: Mod2.-, RTC2.GND, Part4.GND, Part5.GND, TD-er2.GND, Capacitive_Soil_Moisture_Sensor2.GND
  N1: Part4.A3, Capacitive_Soil_Moisture_Sensor2.A
  N2: Part4.D10_PWM/SS, TD-er2.RX
  N3: Part4.D11_PWM/MOSI, TD-er2.TX
  N4: Part4.D2, Part5.DATA
  5V: Part4.5V, TD-er2.Vin

custom parts:
  KY-018 Photoresistor Module: KY-018 Photoresistor module, used to measure light intensity. It can determine the presence or absence of light.
  DS3231 AT24C32 Real Time Clock: Real-time clock basedo on chip DS3231, plus memory chip AT24C32 (32 Kb storage capacity). On-chip temperature sensor with an accuracy of ±3 ℃, I2C bus interface maximum speed: 400 kHz. Operating voltage: 3.3 V to 5.5 V with battery backup capabilities.
  DFRobot Capacitive Soil Moisture Sensor V1.0: DFRobot Capacitive Soil Moisture Sensor V1.0 This product measures soil moisture levels by capacitive sensing, rather than resistive sensing like other types of moisture sensor. It is made of a corrosion resistant material giving it a long service life. Insert it into soil and impress your friends with the real-time soil moisture data! The product includes an on-board voltage regulator which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
